// Logisim project Combinational_Logic_Blocks.circ as structural Verilog
module adder_1_bit (
  input  a,
  input  b,
  input  cin,
  output S,
  output Cout
);

  wire and_1_out, and_2_out, and_3_out;

  xor xor_1 (S, a, b, cin);
  and and_1 (and_1_out, a, b);
  and and_2 (and_2_out, a, cin);
  and and_3 (and_3_out, b, cin);
  or or_1 (Cout, and_1_out, and_2_out, and_3_out);
endmodule

module adder_4_bits (
  input  [3:0] A,
  input  [3:0] B,
  input  Cin,
  output [3:0] S,
  output Cout,
  output Overflow
);

  wire adder_1_bit_1_cout, adder_1_bit_2_cout, adder_1_bit_3_cout;

  // Probe on A
  // Probe on B
  adder_1_bit adder_1_bit_1 (.a(A[0]), .b(B[0]), .cin(Cin), .S(S[0]), .Cout(adder_1_bit_1_cout));
  adder_1_bit adder_1_bit_2 (.a(A[1]), .b(B[1]), .cin(adder_1_bit_1_cout), .S(S[1]), .Cout(adder_1_bit_2_cout));
  // Probe on S
  adder_1_bit adder_1_bit_3 (.a(A[2]), .b(B[2]), .cin(adder_1_bit_2_cout), .S(S[2]), .Cout(adder_1_bit_3_cout));
  adder_1_bit adder_1_bit_4 (.a(A[3]), .b(B[3]), .cin(adder_1_bit_3_cout), .S(S[3]), .Cout(Cout));
  xor xor_1 (Overflow, Cout, adder_1_bit_3_cout);
endmodule

module add_subtract_4_bits (
  input  [3:0] A,
  input  [3:0] B,
  input  Sub,
  output [3:0] S,
  output Cout,
  output Overflow
);

  wire adder_1_bit_1_cout, adder_1_bit_2_cout, adder_1_bit_3_cout, xor_1_out, xor_2_out, xor_3_out, xor_4_out;

  // Probe on B
  // Probe on A
  xor xor_1 (xor_1_out, Sub, B[0]);
  adder_1_bit adder_1_bit_1 (.a(A[0]), .b(xor_1_out), .cin(Sub), .S(S[0]), .Cout(adder_1_bit_1_cout));
  xor xor_2 (xor_2_out, B[1], Sub);
  adder_1_bit adder_1_bit_2 (.a(A[1]), .b(xor_2_out), .cin(adder_1_bit_1_cout), .S(S[1]), .Cout(adder_1_bit_2_cout));
  xor xor_3 (xor_3_out, B[2], Sub);
  // Probe on S
  adder_1_bit adder_1_bit_3 (.a(A[2]), .b(xor_3_out), .cin(adder_1_bit_2_cout), .S(S[2]), .Cout(adder_1_bit_3_cout));
  xor xor_4 (xor_4_out, B[3], Sub);
  adder_1_bit adder_1_bit_4 (.a(A[3]), .b(xor_4_out), .cin(adder_1_bit_3_cout), .S(S[3]), .Cout(Cout));
  xor xor_5 (Overflow, Cout, adder_1_bit_3_cout);
endmodule

module Branch (
  input  [3:0] A,
  input  [3:0] B,
  input  BrUn,
  output BrLT,
  output BrEq
);

  wire comparator_1_eq, comparator_1_lt, comparator_2_eq, comparator_2_lt;

  Comparator #(.width(4)) comparator_1 (.a(A), .b(B), .eq(comparator_1_eq), .lt(comparator_1_lt));  // open: gt
  Comparator #(.mode("unsigned"), .width(4)) comparator_2 (
    .a(A), .b(B), .eq(comparator_2_eq), .lt(comparator_2_lt));  // open: gt
  Multiplexer #(.enable("false")) multiplexer_1 (.in0(comparator_1_lt), .in1(comparator_2_lt), .out(BrLT), .sel(BrUn));
  Multiplexer #(.enable("false")) multiplexer_2 (.in0(comparator_1_eq), .in1(comparator_2_eq), .out(BrEq), .sel(BrUn));
endmodule

module Branch_details (
  input  [3:0] A,
  input  [3:0] B,
  input  BrUn,
  output BrLt,
  output BrEq
);

  wire and_1_out, and_2_out, and_3_out, and_4_out, and_5_out, and_6_out, and_7_out, and_8_out, and_9_out,
       and_10_out, and_11_out, and_12_out, and_13_out, and_14_out, and_15_out, and_16_out, and_17_out,
       and_18_out, and_19_out, and_20_out, and_21_out, and_22_out, and_23_out, and_24_out, and_25_out,
       and_26_out, and_27_out, and_28_out, and_29_out, and_30_out, and_31_out, and_32_out, not_1_out,
       not_2_out, not_3_out, not_4_out, not_5_out, not_6_out, not_7_out, not_8_out, not_9_out;

  not not_1 (not_1_out, A[3]);
  not not_2 (not_2_out, A[2]);
  not not_3 (not_3_out, A[1]);
  not not_4 (not_4_out, A[0]);
  not not_5 (not_5_out, B[3]);
  not not_6 (not_6_out, B[2]);
  not not_7 (not_7_out, B[1]);
  not not_8 (not_8_out, B[0]);
  not not_9 (not_9_out, BrUn);
  and and_1 (and_1_out, not_1_out, not_2_out, not_3_out, not_4_out, not_5_out, B[0]);
  and and_2 (and_2_out, not_1_out, not_2_out, not_3_out, not_5_out, B[1]);
  and and_3 (and_3_out, not_1_out, not_2_out, not_4_out, not_5_out, B[1], B[0]);
  and and_4 (and_4_out, not_1_out, not_2_out, not_5_out, B[2]);
  and and_5 (and_5_out, not_1_out, not_3_out, not_4_out, not_5_out, B[2], B[0]);
  and and_6 (and_6_out, not_1_out, not_3_out, not_5_out, B[2], B[1]);
  and and_7 (and_7_out, not_1_out, not_4_out, not_5_out, B[2], B[1], B[0]);
  and and_8 (and_8_out, not_1_out, B[3], BrUn);
  and and_9 (and_9_out, A[3], not_5_out, not_9_out);
  and and_10 (and_10_out, A[3], not_2_out, not_3_out, not_4_out, B[3], B[0]);
  and and_11 (and_11_out, A[3], not_2_out, not_3_out, B[3], B[1]);
  and and_12 (and_12_out, A[3], not_2_out, not_4_out, B[3], B[1], B[0]);
  and and_13 (and_13_out, A[3], not_2_out, B[3], B[2]);
  and and_14 (and_14_out, A[3], not_3_out, not_4_out, B[3], B[2], B[0]);
  and and_15 (and_15_out, A[3], not_3_out, B[3], B[2], B[1]);
  and and_16 (and_16_out, A[3], not_4_out, B[3], B[2], B[1], B[0]);
  and and_17 (and_17_out, not_1_out, not_2_out, not_3_out, not_4_out, not_5_out, not_6_out, not_7_out, not_8_out);
  and and_18 (and_18_out, not_1_out, not_2_out, not_3_out, A[0], not_5_out, not_6_out, not_7_out, B[0]);
  and and_19 (and_19_out, not_1_out, not_2_out, A[1], not_4_out, not_5_out, not_6_out, B[1], not_8_out);
  and and_20 (and_20_out, not_1_out, not_2_out, A[1], A[0], not_5_out, not_6_out, B[1], B[0]);
  and and_21 (and_21_out, not_1_out, A[2], not_3_out, not_4_out, not_5_out, B[2], not_7_out, not_8_out);
  and and_22 (and_22_out, not_1_out, A[2], not_3_out, A[0], not_5_out, B[2], not_7_out, B[0]);
  and and_23 (and_23_out, not_1_out, A[2], A[1], not_4_out, not_5_out, B[2], B[1], not_8_out);
  and and_24 (and_24_out, not_1_out, A[2], A[1], A[0], not_5_out, B[2], B[1], B[0]);
  and and_25 (and_25_out, A[3], not_2_out, not_3_out, not_4_out, B[3], not_6_out, not_7_out, not_8_out);
  and and_26 (and_26_out, A[3], not_2_out, not_3_out, A[0], B[3], not_6_out, not_7_out, B[0]);
  and and_27 (and_27_out, A[3], not_2_out, A[1], not_4_out, B[3], not_6_out, B[1], not_8_out);
  and and_28 (and_28_out, A[3], not_2_out, A[1], A[0], B[3], not_6_out, B[1], B[0]);
  and and_29 (and_29_out, A[3], A[2], not_3_out, not_4_out, B[3], B[2], not_7_out, not_8_out);
  and and_30 (and_30_out, A[3], A[2], not_3_out, A[0], B[3], B[2], not_7_out, B[0]);
  and and_31 (and_31_out, A[3], A[2], A[1], not_4_out, B[3], B[2], B[1], not_8_out);
  and and_32 (and_32_out, A[3], A[2], A[1], A[0], B[3], B[2], B[1], B[0]);
  or or_1 (BrLt, and_1_out, and_2_out, and_3_out, and_4_out, and_5_out, and_6_out, and_7_out, and_8_out, and_9_out, and_10_out, and_11_out, and_12_out, and_13_out, and_14_out, and_15_out, and_16_out);
  or or_2 (BrEq, and_17_out, and_18_out, and_19_out, and_20_out, and_21_out, and_22_out, and_23_out, and_24_out, and_25_out, and_26_out, and_27_out, and_28_out, and_29_out, and_30_out, and_31_out, and_32_out);
endmodule

module adder_1_bit_details (
  input  a,
  input  b,
  input  cin,
  output S,
  output Cout
);

  wire and_1_out, and_2_out, and_3_out, and_4_out, and_5_out, and_6_out, and_7_out, not_1_out, not_2_out,
       not_3_out;

  not not_1 (not_1_out, a);
  not not_2 (not_2_out, b);
  not not_3 (not_3_out, cin);
  and and_1 (and_1_out, not_1_out, not_2_out, cin);
  and and_2 (and_2_out, not_1_out, b, not_3_out);
  and and_3 (and_3_out, a, not_2_out, not_3_out);
  and and_4 (and_4_out, a, b, cin);
  and and_5 (and_5_out, b, cin);
  and and_6 (and_6_out, a, cin);
  and and_7 (and_7_out, a, b);
  or or_1 (S, and_1_out, and_2_out, and_3_out, and_4_out);
  or or_2 (Cout, and_5_out, and_6_out, and_7_out);
endmodule

module rv32_addr_decoder (
  input  [31:0] Inst,
  input  BrEq,
  input  BrLT,
  output R_Type,
  output ADD,
  output SUB,
  output BrUn
);

  wire and_2_out, not_1_out, not_2_out;
  wire [31:0] not_3_out;

  not not_1 (not_1_out, BrEq);
  not not_2 (not_2_out, BrLT);
  assign not_3_out = ~Inst;  // NOT_Gate not_3, 32 bits wide
  and and_1 (R_Type, not_3_out[2], not_3_out[3], Inst[4], Inst[5], not_3_out[6]);
  and and_2 (and_2_out, R_Type, not_3_out[12], not_3_out[13], not_3_out[14]);
  and and_3 (ADD, and_2_out, not_3_out[30]);
  and and_4 (SUB, and_2_out, Inst[30]);
  and and_5 (BrUn, not_3_out[2], not_3_out[3], not_3_out[4], Inst[5], Inst[6], Inst[30]);
endmodule

module ALU_4bit (
  input  [3:0] A,
  input  [3:0] B,
  input  [1:0] S,
  output Overflow,
  output [3:0] R
);

  wire [3:0] add_subtract_4_bits_1_s, and_1_out, multiplexer_1_out, or_1_out;

  // Probe on A
  // Probe on B
  assign and_1_out = A & B;  // AND_Gate and_1, 4 bits wide
  assign or_1_out = A | B;  // OR_Gate or_1, 4 bits wide
  add_subtract_4_bits add_subtract_4_bits_1 (
    .A(A), .B(B), .Sub(S[0]), .S(add_subtract_4_bits_1_s), .Overflow(Overflow));  // open: Cout
  Multiplexer #(.enable("false"), .width(4)) multiplexer_1 (
    .in0(and_1_out), .in1(or_1_out), .out(multiplexer_1_out), .sel(S[0]));
  Multiplexer #(.enable("false"), .width(4)) multiplexer_2 (
    .in0(add_subtract_4_bits_1_s), .in1(multiplexer_1_out), .out(R), .sel(S[1]));
  // Probe on R
endmodule

module mux2 (
  input  A,
  input  B,
  input  S,
  output C
);

  Multiplexer #(.enable("false")) multiplexer_1 (.in0(A), .in1(B), .out(C), .sel(S));
endmodule

module mux4 (
  input  A,
  input  B,
  input  C,
  input  D,
  input  [1:0] S,
  output E,
  output F
);

  wire multiplexer_1_out, multiplexer_2_out;

  // Probe on S
  Multiplexer #(.enable("false")) multiplexer_1 (.in0(A), .in1(B), .out(multiplexer_1_out), .sel(S[0]));
  Multiplexer #(.enable("false")) multiplexer_2 (.in0(C), .in1(D), .out(multiplexer_2_out), .sel(S[0]));
  Multiplexer #(.enable("false")) multiplexer_3 (.in0(multiplexer_1_out), .in1(multiplexer_2_out), .out(E), .sel(S[1]));
  Multiplexer #(.enable("false"), .select(2)) multiplexer_4 (.in0(A), .in1(B), .in2(C), .in3(D), .out(F), .sel(S));
endmodule

module mux2_basic (
  input  A,
  input  B,
  input  S,
  output C
);

  wire and_1_out, and_2_out;

  and and_1 (and_1_out, A, ~S);  // AND_Gate
  and and_2 (and_2_out, B, S);
  or or_1 (C, and_1_out, and_2_out);
endmodule

module rv32_control_CL (
  input  [31:0] Inst,
  input  BrEq,
  input  BrLT,
  output BrUn,
  output MemRW,
  output BSel,
  output [3:0] ALUSel
);

  wire and_2_out, and_4_out;

  and and_1 (BrUn, Inst[13], Inst[6], Inst[5]);
  // Probe on and_2_out
  and and_2 (and_2_out, Inst[1], Inst[0]);
  and and_3 (MemRW, ~Inst[6], Inst[5], ~Inst[4], ~Inst[3], ~Inst[2], and_2_out);  // AND_Gate
  and and_4 (and_4_out, and_2_out, ~Inst[6], Inst[5], Inst[4], ~Inst[3], ~Inst[2]);  // AND_Gate
  not not_1 (BSel, and_4_out);
  Multiplexer #(.enable("false"), .width(4)) multiplexer_1 (
    .in0({Inst[14:12], Inst[30]}), .in1(4'b0000), .out(ALUSel), .sel(BSel));
endmodule

module rv32_control_ROM (
  input  [31:0] Inst,
  input  BrEq,
  input  BrLT,
  output PCSel,
  output [2:0] ImmSel,
  output BrUn,
  output Asel,
  output BSel,
  output [3:0] ALUSel,
  output MemRW,
  output RegWEn,
  output [1:0] WBSel
);

  // Probe on {BrEq, BrLT, Inst[30], Inst[14:12], Inst[6:2]}
  ROM #(.addrWidth(11), .dataWidth(15)) rom_1 (
    .addr({BrEq, BrLT, Inst[30], Inst[14:12], Inst[6:2]}),
    .data({PCSel, ImmSel, BrUn, Asel, BSel, ALUSel, MemRW, RegWEn, WBSel}));
  // Probe on {PCSel, ImmSel, BrUn, Asel, BSel, ALUSel, MemRW, RegWEn, WBSel}

  // Notes on the sheet:
  //   contents of rom_1 (hex, n*v repeats v):
  //   4*0 105 7*0 5 11*0 2300 19*0 25 19*0 104 7*0 908 195*0 15 255*0 5 255*0 15 255*0 5 11*0 5300 243*0
  //   15 255*0 5 255*0 15
endmodule

module ALU_32 (
  input  [31:0] A,
  input  [31:0] B,
  input  [3:0] S,
  output [31:0] R
);

  wire [0:0] comparator_1_lt, comparator_2_lt;
  wire [31:0] adder_1_out, and_1_out, or_1_out, shifter_1_out, shifter_2_out, shifter_3_out,
       subtractor_1_out, xor_1_out;

  Comparator #(.width(32)) comparator_1 (.a(A), .b(B), .lt(comparator_1_lt[0]));  // open: gt, eq
  Comparator #(.mode("unsigned"), .width(32)) comparator_2 (.a(A), .b(B), .lt(comparator_2_lt[0]));  // open: gt, eq
  Adder #(.width(32)) adder_1 (.a(A), .b(B), .out(adder_1_out));  // open: cin, cout
  Subtractor #(.width(32)) subtractor_1 (.a(A), .b(B), .out(subtractor_1_out));  // open: bin, bout
  Shifter #(.width(32)) shifter_1 (.in(A), .\dist (B[4:0]), .out(shifter_1_out));
  assign xor_1_out = A ^ B;  // XOR_Gate xor_1, 32 bits wide
  Shifter #(.shift("lr"), .width(32)) shifter_2 (.in(A), .\dist (B[4:0]), .out(shifter_2_out));
  Shifter #(.shift("ar"), .width(32)) shifter_3 (.in(A), .\dist (B[4:0]), .out(shifter_3_out));
  assign or_1_out = A | B;  // OR_Gate or_1, 32 bits wide
  assign and_1_out = A & B;  // AND_Gate and_1, 32 bits wide
  Multiplexer #(.enable("false"), .select(4), .width(32)) multiplexer_1 (
    .in0(adder_1_out), .in1(subtractor_1_out), .in2(shifter_1_out), .in3(shifter_1_out),
    .in4({{31{1'b0}}, comparator_1_lt[0]}), .in5({{31{1'b0}}, comparator_1_lt[0]}),
    .in6({{31{1'b0}}, comparator_2_lt[0]}), .in7({{31{1'b0}}, comparator_2_lt[0]}), .in8(xor_1_out),
    .in9(xor_1_out), .in10(shifter_2_out), .in11(shifter_3_out), .in12(or_1_out), .in13(or_1_out),
    .in14(and_1_out), .in15(and_1_out), .out(R), .sel(S));

  // Notes on the sheet:
  //   SLT
  //   SLTU
  //   SLL
  //   SRL
  //   SRA
  //   S=inst[14,13,12,30]
endmodule

module ImmGen (
  input  [11:0] Imm,
  input  [2:0] ImmSel,
  output [31:0] ExtImm
);

  wire [19:0] multiplexer_1_out;

  // Probe on Imm
  Multiplexer #(.enable("false"), .width(20)) multiplexer_1 (
    .in0({20{1'b0}}), .in1({20{1'b1}}), .out(multiplexer_1_out), .sel(Imm[11]));
  // Probe on ExtImm
  Multiplexer #(.enable("false"), .select(3), .width(32)) multiplexer_2 (
    .in0({multiplexer_1_out, Imm}), .out(ExtImm), .sel(ImmSel));  // open: in1, in2, in3, in4, in5, in6, in7
endmodule

module regfile_32x32_reset (
  input  [31:0] DataD,
  input  [4:0] AddrD,
  input  [4:0] AddrA,
  input  [4:0] AddrB,
  input  RegWEn,
  input  clk,
  input  Reset,
  output [31:0] Reg_rs1,
  output [31:0] x0,
  output [31:0] x1,
  output [31:0] x2,
  output [31:0] x3,
  output [31:0] x4,
  output [31:0] x5,
  output [31:0] x6,
  output [31:0] x7,
  output [31:0] Reg_rs2,
  output [31:0] x8,
  output [31:0] x9,
  output [31:0] x10,
  output [31:0] x11,
  output [31:0] x12,
  output [31:0] x13,
  output [31:0] x14,
  output [31:0] x15
);

  wire demultiplexer_1_out1, demultiplexer_1_out2, demultiplexer_1_out3, demultiplexer_1_out4,
       demultiplexer_1_out5, demultiplexer_1_out6, demultiplexer_1_out7, demultiplexer_1_out8,
       demultiplexer_1_out9, demultiplexer_1_out10, demultiplexer_1_out11, demultiplexer_1_out12,
       demultiplexer_1_out13, demultiplexer_1_out14, demultiplexer_1_out15, demultiplexer_1_out16,
       demultiplexer_1_out17, demultiplexer_1_out18, demultiplexer_1_out19, demultiplexer_1_out20,
       demultiplexer_1_out21, demultiplexer_1_out22, demultiplexer_1_out23, demultiplexer_1_out24,
       demultiplexer_1_out25, demultiplexer_1_out26, demultiplexer_1_out27, demultiplexer_1_out28,
       demultiplexer_1_out29, demultiplexer_1_out30, demultiplexer_1_out31;
  wire [31:0] register_14_q, register_15_q, register_16_q, register_17_q, register_18_q, register_19_q,
       register_20_q, register_21_q, register_22_q, register_23_q, register_24_q, register_25_q,
       register_26_q, register_27_q, register_28_q, register_29_q;

  Register #(.width(32)) rx1 (.D(DataD), .en(demultiplexer_1_out1), .clk(clk), .Q(x1), .clr(Reset));
  Register #(.width(32)) rx2 (.D(DataD), .en(demultiplexer_1_out2), .clk(clk), .Q(x2), .clr(Reset));
  Register #(.width(32)) register_1 (.D(DataD), .en(demultiplexer_1_out3), .clk(clk), .Q(x3), .clr(Reset));
  Register #(.width(32)) register_2 (.D(DataD), .en(demultiplexer_1_out4), .clk(clk), .Q(x4), .clr(Reset));
  Register #(.width(32)) register_3 (.D(DataD), .en(demultiplexer_1_out5), .clk(clk), .Q(x5), .clr(Reset));
  Register #(.width(32)) register_4 (.D(DataD), .en(demultiplexer_1_out6), .clk(clk), .Q(x6), .clr(Reset));
  Register #(.width(32)) register_5 (.D(DataD), .en(demultiplexer_1_out7), .clk(clk), .Q(x7), .clr(Reset));
  Demultiplexer #(.enable("false"), .select(5)) demultiplexer_1 (
    .out1(demultiplexer_1_out1), .out2(demultiplexer_1_out2), .out3(demultiplexer_1_out3),
    .out4(demultiplexer_1_out4), .out5(demultiplexer_1_out5), .out6(demultiplexer_1_out6),
    .out7(demultiplexer_1_out7), .out8(demultiplexer_1_out8), .out9(demultiplexer_1_out9),
    .out10(demultiplexer_1_out10), .out11(demultiplexer_1_out11), .out12(demultiplexer_1_out12),
    .out13(demultiplexer_1_out13), .out14(demultiplexer_1_out14), .out15(demultiplexer_1_out15),
    .out16(demultiplexer_1_out16), .out17(demultiplexer_1_out17), .out18(demultiplexer_1_out18),
    .out19(demultiplexer_1_out19), .out20(demultiplexer_1_out20), .out21(demultiplexer_1_out21),
    .out22(demultiplexer_1_out22), .out23(demultiplexer_1_out23), .out24(demultiplexer_1_out24),
    .out25(demultiplexer_1_out25), .out26(demultiplexer_1_out26), .out27(demultiplexer_1_out27),
    .out28(demultiplexer_1_out28), .out29(demultiplexer_1_out29), .out30(demultiplexer_1_out30),
    .out31(demultiplexer_1_out31), .in(RegWEn), .sel(AddrD));  // open: out0
  Multiplexer #(.enable("false"), .select(5), .width(32)) multiplexer_1 (
    .in0({32{1'b0}}), .in1(x1), .in2(x2), .in3(x3), .in4(x4), .in5(x5), .in6(x6), .in7(x7), .in8(x8),
    .in9(x9), .in10(x10), .in11(x11), .in12(x12), .in13(x13), .in14(x14), .in15(x15), .in16(register_14_q),
    .in17(register_15_q), .in18(register_16_q), .in19(register_17_q), .in20(register_18_q),
    .in21(register_19_q), .in22(register_20_q), .in23(register_21_q), .in24(register_22_q),
    .in25(register_23_q), .in26(register_24_q), .in27(register_25_q), .in28(register_26_q),
    .in29(register_27_q), .in30(register_28_q), .in31(register_29_q), .out(Reg_rs1), .sel(AddrA));
  Register #(.width(32)) register_6 (.D(DataD), .en(demultiplexer_1_out8), .clk(clk), .Q(x8), .clr(Reset));
  Register #(.width(32)) register_7 (.D(DataD), .en(demultiplexer_1_out9), .clk(clk), .Q(x9), .clr(Reset));
  Register #(.width(32)) register_8 (.D(DataD), .en(demultiplexer_1_out10), .clk(clk), .Q(x10), .clr(Reset));
  Register #(.width(32)) register_9 (.D(DataD), .en(demultiplexer_1_out11), .clk(clk), .Q(x11), .clr(Reset));
  Register #(.width(32)) register_10 (.D(DataD), .en(demultiplexer_1_out12), .clk(clk), .Q(x12), .clr(Reset));
  Register #(.width(32)) register_11 (.D(DataD), .en(demultiplexer_1_out13), .clk(clk), .Q(x13), .clr(Reset));
  Register #(.width(32)) register_12 (.D(DataD), .en(demultiplexer_1_out14), .clk(clk), .Q(x14), .clr(Reset));
  Register #(.width(32)) register_13 (.D(DataD), .en(demultiplexer_1_out15), .clk(clk), .Q(x15), .clr(Reset));
  Register #(.width(32)) register_14 (.D(DataD), .en(demultiplexer_1_out16), .clk(clk), .Q(register_14_q), .clr(Reset));
  Register #(.width(32)) register_15 (.D(DataD), .en(demultiplexer_1_out17), .clk(clk), .Q(register_15_q), .clr(Reset));
  Register #(.width(32)) register_16 (.D(DataD), .en(demultiplexer_1_out18), .clk(clk), .Q(register_16_q), .clr(Reset));
  Register #(.width(32)) register_17 (.D(DataD), .en(demultiplexer_1_out19), .clk(clk), .Q(register_17_q), .clr(Reset));
  Register #(.width(32)) register_18 (.D(DataD), .en(demultiplexer_1_out20), .clk(clk), .Q(register_18_q), .clr(Reset));
  Register #(.width(32)) register_19 (.D(DataD), .en(demultiplexer_1_out21), .clk(clk), .Q(register_19_q), .clr(Reset));
  Register #(.width(32)) register_20 (.D(DataD), .en(demultiplexer_1_out22), .clk(clk), .Q(register_20_q), .clr(Reset));
  Register #(.width(32)) register_21 (.D(DataD), .en(demultiplexer_1_out23), .clk(clk), .Q(register_21_q), .clr(Reset));
  Multiplexer #(.enable("false"), .select(5), .width(32)) multiplexer_2 (
    .in0({32{1'b0}}), .in1(x1), .in2(x2), .in3(x3), .in4(x4), .in5(x5), .in6(x6), .in7(x7), .in8(x8),
    .in9(x9), .in10(x10), .in11(x11), .in12(x12), .in13(x13), .in14(x14), .in15(x15), .in16(register_14_q),
    .in17(register_15_q), .in18(register_16_q), .in19(register_17_q), .in20(register_18_q),
    .in21(register_19_q), .in22(register_20_q), .in23(register_21_q), .in24(register_22_q),
    .in25(register_23_q), .in26(register_24_q), .in27(register_25_q), .in28(register_26_q),
    .in29(register_27_q), .in30(register_28_q), .in31(register_29_q), .out(Reg_rs2), .sel(AddrB));
  Register #(.width(32)) register_22 (.D(DataD), .en(demultiplexer_1_out24), .clk(clk), .Q(register_22_q), .clr(Reset));
  Register #(.width(32)) register_23 (.D(DataD), .en(demultiplexer_1_out25), .clk(clk), .Q(register_23_q), .clr(Reset));
  Register #(.width(32)) register_24 (.D(DataD), .en(demultiplexer_1_out26), .clk(clk), .Q(register_24_q), .clr(Reset));
  Register #(.width(32)) register_25 (.D(DataD), .en(demultiplexer_1_out27), .clk(clk), .Q(register_25_q), .clr(Reset));
  Register #(.width(32)) register_26 (.D(DataD), .en(demultiplexer_1_out28), .clk(clk), .Q(register_26_q), .clr(Reset));
  Register #(.width(32)) register_27 (.D(DataD), .en(demultiplexer_1_out29), .clk(clk), .Q(register_27_q), .clr(Reset));
  Register #(.width(32)) register_28 (.D(DataD), .en(demultiplexer_1_out30), .clk(clk), .Q(register_28_q), .clr(Reset));
  Register #(.width(32)) register_29 (.D(DataD), .en(demultiplexer_1_out31), .clk(clk), .Q(register_29_q), .clr(Reset));

  assign x0 = {32{1'b0}};

  // Notes on the sheet:
  //   reg0 is always 0
endmodule

module rv32_v1 (
  input  Reset,
  input  [2:0] ImmSel,
  input  RegWEn,
  input  BSel,
  input  [3:0] ALUSel,
  output [31:0] out_6,
  output [31:0] out_7,
  output [31:0] out_8,
  output [31:0] out_9,
  output [31:0] out_10,
  output [31:0] out_11,
  output [31:0] out_12,
  output [31:0] out_13,
  output [31:0] out_14,
  output [31:0] out_15,
  output [31:0] out_16,
  output [31:0] out_17,
  output [31:0] out_18,
  output [31:0] out_19,
  output [31:0] out_20,
  output [31:0] out_21
);

  wire CLK;
  wire [7:0] adder_1_out, register_1_q;
  wire [31:0] alu_32_1_r, immgen_1_extimm, multiplexer_1_out, regfile_32x32_reset_1_reg_rs1,
       regfile_32x32_reset_1_reg_rs2, rom_1_data;

  Clock u_CLK (.out(CLK));
  Register register_1 (.D(adder_1_out), .clk(CLK), .Q(register_1_q), .clr(Reset));  // open: en
  // Probe on adder_1_out
  ROM #(.dataWidth(32)) rom_1 (.addr(register_1_q), .data(rom_1_data));
  // Probe on register_1_q
  Adder adder_1 (.a(8'h1), .b(register_1_q), .out(adder_1_out));  // open: cin, cout
  // Probe on rom_1_data
  // Probe on rom_1_data[11:7]
  // Probe on rom_1_data[19:15]
  // Probe on rom_1_data[24:20]
  // Probe on rom_1_data[31:20]
  regfile_32x32_reset regfile_32x32_reset_1 (
    .DataD(alu_32_1_r), .AddrD(rom_1_data[11:7]), .AddrA(rom_1_data[19:15]), .AddrB(rom_1_data[24:20]),
    .RegWEn(RegWEn), .clk(CLK), .Reset(Reset), .Reg_rs1(regfile_32x32_reset_1_reg_rs1), .x0(out_6),
    .x1(out_7), .x2(out_8), .x3(out_9), .x4(out_10), .x5(out_11), .x6(out_12), .x7(out_13),
    .Reg_rs2(regfile_32x32_reset_1_reg_rs2), .x8(out_14), .x9(out_15), .x10(out_16), .x11(out_17),
    .x12(out_18), .x13(out_19), .x14(out_20), .x15(out_21));
  ImmGen immgen_1 (.Imm(rom_1_data[31:20]), .ImmSel(ImmSel), .ExtImm(immgen_1_extimm));
  // Probe on regfile_32x32_reset_1_reg_rs1
  // Probe on regfile_32x32_reset_1_reg_rs2
  // Probe on immgen_1_extimm
  Multiplexer #(.enable("false"), .width(32)) multiplexer_1 (
    .in0(regfile_32x32_reset_1_reg_rs2), .in1(immgen_1_extimm), .out(multiplexer_1_out), .sel(BSel));
  // Probe on multiplexer_1_out
  ALU_32 alu_32_1 (.A(regfile_32x32_reset_1_reg_rs1), .B(multiplexer_1_out), .S(ALUSel), .R(alu_32_1_r));
  // Probe on alu_32_1_r

  // Other names for the same wires on the sheet: x0[31:0] = out_6; x1[31:0] = out_7; x2[31:0] = out_8;
  //   x3[31:0] = out_9; x4[31:0] = out_10; x5[31:0] = out_11; x6[31:0] = out_12; x7[31:0] = out_13; x8[31:0] = out_14;
  //   x9[31:0] = out_15; x10[31:0] = out_16; x11[31:0] = out_17; x12[31:0] = out_18; x13[31:0] = out_19;
  //   x14[31:0] = out_20; x15[31:0] = out_21

  // Notes on the sheet:
  //   Control Signals
  //   contents of rom_1 (hex, n*v repeats v):
  //   500113 200193 600393 ff700493 3100b3 938333 608233 403100b3 3110b3 9140b3 4030d233 13
  //   v1: R- and I- Types
endmodule

module rv32_v2 (
  input  Reset,
  input  in_2,
  input  [2:0] ImmSel,
  input  RegWEn,
  input  BSel,
  input  [3:0] ALUSel,
  input  MemRW,
  input  WBSel,
  output [31:0] out_9,
  output [31:0] out_10,
  output [31:0] out_11,
  output [31:0] out_12,
  output [31:0] out_13,
  output [31:0] out_14,
  output [31:0] out_15,
  output [31:0] out_16,
  output [31:0] out_17,
  output [31:0] out_18,
  output [31:0] out_19,
  output [31:0] out_20,
  output [31:0] out_21,
  output [31:0] out_22,
  output [31:0] out_23,
  output [31:0] out_24
);

  wire CLK;
  wire [7:0] adder_1_out, register_1_q;
  wire [31:0] alu_32_1_r, DMEM_dout, immgen_1_extimm, multiplexer_1_out, multiplexer_2_out,
       regfile_32x32_reset_1_reg_rs1, regfile_32x32_reset_1_reg_rs2, rom_1_data;

  Clock u_CLK (.out(CLK));
  Register register_1 (.D(adder_1_out), .clk(CLK), .Q(register_1_q), .clr(Reset));  // open: en
  // Probe on adder_1_out
  ROM #(.dataWidth(32)) rom_1 (.addr(register_1_q), .data(rom_1_data));
  // Probe on register_1_q
  Adder adder_1 (.a(8'h1), .b(register_1_q), .out(adder_1_out));  // open: cin, cout
  // Probe on rom_1_data
  // Probe on rom_1_data[11:7]
  // Probe on rom_1_data[19:15]
  // Probe on rom_1_data[24:20]
  // Probe on rom_1_data[31:20]
  regfile_32x32_reset regfile_32x32_reset_1 (
    .DataD(multiplexer_2_out), .AddrD(rom_1_data[11:7]), .AddrA(rom_1_data[19:15]),
    .AddrB(rom_1_data[24:20]), .RegWEn(RegWEn), .clk(CLK), .Reset(Reset),
    .Reg_rs1(regfile_32x32_reset_1_reg_rs1), .x0(out_9), .x1(out_10), .x2(out_11), .x3(out_12), .x4(out_13),
    .x5(out_14), .x6(out_15), .x7(out_16), .Reg_rs2(regfile_32x32_reset_1_reg_rs2), .x8(out_17), .x9(out_18),
    .x10(out_19), .x11(out_20), .x12(out_21), .x13(out_22), .x14(out_23), .x15(out_24));
  ImmGen immgen_1 (.Imm(rom_1_data[31:20]), .ImmSel(ImmSel), .ExtImm(immgen_1_extimm));
  // Probe on regfile_32x32_reset_1_reg_rs1
  // Probe on regfile_32x32_reset_1_reg_rs2
  // Probe on immgen_1_extimm
  Multiplexer #(.enable("false"), .width(32)) multiplexer_1 (
    .in0(regfile_32x32_reset_1_reg_rs2), .in1(immgen_1_extimm), .out(multiplexer_1_out), .sel(BSel));
  // Probe on multiplexer_1_out
  // Probe on multiplexer_2_out
  ALU_32 alu_32_1 (.A(regfile_32x32_reset_1_reg_rs1), .B(multiplexer_1_out), .S(ALUSel), .R(alu_32_1_r));
  // Probe on alu_32_1_r
  // Probe on alu_32_1_r[9:2]
  RAM #(.asyncread("true"), .dataWidth(32)) DMEM (
    .addr(alu_32_1_r[9:2]), .we(MemRW), .oe(in_2), .clk(CLK), .dout(DMEM_dout));  // open: din
  Multiplexer #(.enable("false"), .width(32)) multiplexer_2 (
    .in0(DMEM_dout), .in1(alu_32_1_r), .out(multiplexer_2_out), .sel(WBSel));

  // Other names for the same wires on the sheet: x0[31:0] = out_9; x1[31:0] = out_10; x2[31:0] = out_11;
  //   x3[31:0] = out_12; x4[31:0] = out_13; x5[31:0] = out_14; x6[31:0] = out_15; x7[31:0] = out_16;
  //   x8[31:0] = out_17; x9[31:0] = out_18; x10[31:0] = out_19; x11[31:0] = out_20; x12[31:0] = out_21;
  //   x13[31:0] = out_22; x14[31:0] = out_23; x15[31:0] = out_24

  // Notes on the sheet:
  //   Control Signals
  //   contents of rom_1 (hex, n*v repeats v):
  //   2083 402103 2081b3 13
  //   v2: R and ITypes (imm, load)
  //   Only lw, no lb or lh since word (not byte) address is used by RAM
endmodule

module rv32_v3_store (
  input  Reset,
  input  [2:0] ImmSel,
  input  RegWEn,
  input  BSel,
  input  [3:0] ALUSel,
  input  MemRW,
  input  WBSel,
  output [31:0] out_8,
  output [31:0] out_9,
  output [31:0] out_10,
  output [31:0] out_11,
  output [31:0] out_12,
  output [31:0] out_13,
  output [31:0] out_14,
  output [31:0] out_15,
  output [31:0] out_16,
  output [31:0] out_17,
  output [31:0] out_18,
  output [31:0] out_19,
  output [31:0] out_20,
  output [31:0] out_21,
  output [31:0] out_22,
  output [31:0] out_23
);

  wire CLK;
  wire [7:0] adder_1_out, register_1_q;
  wire [31:0] alu_32_1_r, DMEM_dout, immgen_v2_1_extimm, multiplexer_1_out, multiplexer_2_out,
       regfile_32x32_reset_1_reg_rs1, regfile_32x32_reset_1_reg_rs2, rom_1_data;

  Clock u_CLK (.out(CLK));
  Register register_1 (.D(adder_1_out), .clk(CLK), .Q(register_1_q), .clr(Reset));  // open: en
  // Probe on adder_1_out
  ROM #(.dataWidth(32)) rom_1 (.addr(register_1_q), .data(rom_1_data));
  // Probe on register_1_q
  Adder adder_1 (.a(8'h1), .b(register_1_q), .out(adder_1_out));  // open: cin, cout
  // Probe on rom_1_data
  // Probe on rom_1_data[11:7]
  // Probe on rom_1_data[19:15]
  // Probe on rom_1_data[24:20]
  // Probe on multiplexer_2_out
  regfile_32x32_reset regfile_32x32_reset_1 (
    .DataD(multiplexer_2_out), .AddrD(rom_1_data[11:7]), .AddrA(rom_1_data[19:15]),
    .AddrB(rom_1_data[24:20]), .RegWEn(RegWEn), .clk(CLK), .Reset(Reset),
    .Reg_rs1(regfile_32x32_reset_1_reg_rs1), .x0(out_8), .x1(out_9), .x2(out_10), .x3(out_11), .x4(out_12),
    .x5(out_13), .x6(out_14), .x7(out_15), .Reg_rs2(regfile_32x32_reset_1_reg_rs2), .x8(out_16), .x9(out_17),
    .x10(out_18), .x11(out_19), .x12(out_20), .x13(out_21), .x14(out_22), .x15(out_23));
  ImmGen_v2 immgen_v2_1 (.Inst(rom_1_data), .ImmSel(ImmSel), .ExtImm(immgen_v2_1_extimm));
  // Probe on regfile_32x32_reset_1_reg_rs1
  // Probe on regfile_32x32_reset_1_reg_rs2
  // Probe on immgen_v2_1_extimm
  Multiplexer #(.enable("false"), .width(32)) multiplexer_1 (
    .in0(regfile_32x32_reset_1_reg_rs2), .in1(immgen_v2_1_extimm), .out(multiplexer_1_out), .sel(BSel));
  // Probe on multiplexer_1_out
  ALU_32 alu_32_1 (.A(regfile_32x32_reset_1_reg_rs1), .B(multiplexer_1_out), .S(ALUSel), .R(alu_32_1_r));
  // Probe on alu_32_1_r
  // Probe on alu_32_1_r[9:2]
  RAM #(.asyncread("true"), .dataWidth(32)) DMEM (
    .addr(alu_32_1_r[9:2]), .we(MemRW), .oe(1'b1), .clk(CLK), .din(regfile_32x32_reset_1_reg_rs2),
    .dout(DMEM_dout));
  Multiplexer #(.enable("false"), .width(32)) multiplexer_2 (
    .in0(DMEM_dout), .in1(alu_32_1_r), .out(multiplexer_2_out), .sel(WBSel));
  // Probe on DMEM_dout

  // Other names for the same wires on the sheet: x0[31:0] = out_8; x1[31:0] = out_9; x2[31:0] = out_10;
  //   x3[31:0] = out_11; x4[31:0] = out_12; x5[31:0] = out_13; x6[31:0] = out_14; x7[31:0] = out_15;
  //   x8[31:0] = out_16; x9[31:0] = out_17; x10[31:0] = out_18; x11[31:0] = out_19; x12[31:0] = out_20;
  //   x13[31:0] = out_21; x14[31:0] = out_22; x15[31:0] = out_23

  // Notes on the sheet:
  //   Control Signals
  //   contents of rom_1 (hex, n*v repeats v):
  //   12300093 409113 102023 202223 2183 402203 4182b3 13
  //   Only lw, no lb or lh since word (not byte) address is used by RAM
endmodule

module ImmGen_v2 (
  input  [31:0] Inst,
  input  [2:0] ImmSel,
  output [31:0] ExtImm
);

  wire [11:0] multiplexer_1_out;
  wire [19:0] multiplexer_2_out;

  Multiplexer #(.enable("false"), .width(12)) multiplexer_1 (
    .in0(Inst[31:20]), .in1({Inst[31:25], Inst[11:7]}), .out(multiplexer_1_out), .sel(ImmSel[0]));
  Multiplexer #(.enable("false"), .width(20)) multiplexer_2 (
    .in0({20{1'b0}}), .in1({20{1'b1}}), .out(multiplexer_2_out), .sel(multiplexer_1_out[11]));
  Multiplexer #(.enable("false"), .select(3), .width(32)) multiplexer_3 (
    .in0({multiplexer_2_out, multiplexer_1_out}), .in1({multiplexer_2_out, multiplexer_1_out}), .out(ExtImm),
    .sel(ImmSel));  // open: in2, in3, in4, in5, in6, in7

  // Notes on the sheet:
  //   Hence, we need to divide RV32 offset by 4.
  //   When ImmSel=010, we calculate the offset to PC. For Logisim, PC is by default incremented by 1, not 4.
endmodule

module rv32_v4_branch (
  input  Reset,
  input  PCSel,
  input  [2:0] ImmSel,
  input  BrUn,
  input  ASel,
  input  BSel,
  input  [3:0] ALUSel,
  input  MemRW,
  input  RegWEn,
  input  WBSel,
  output [31:0] out_11,
  output [31:0] out_12,
  output [31:0] out_13,
  output [31:0] out_14,
  output [31:0] out_15,
  output [31:0] out_16,
  output [31:0] out_17,
  output [31:0] out_18,
  output [31:0] out_19,
  output [31:0] out_20,
  output [31:0] out_21,
  output [31:0] out_22,
  output [31:0] out_23,
  output BrEq,
  output [31:0] out_25,
  output BrLT,
  output [31:0] out_27,
  output [31:0] out_28
);

  wire CLK;
  wire [7:0] adder_1_out, multiplexer_1_out, register_1_q;
  wire [31:0] alu_32_1_r, DMEM_dout, immgen_v3_1_extimm, multiplexer_2_out, multiplexer_3_out,
       multiplexer_4_out, regfile_32x32_reset_1_reg_rs1, regfile_32x32_reset_1_reg_rs2, rom_1_data;

  // Probe on alu_32_1_r
  Multiplexer #(.enable("false"), .width(8)) multiplexer_1 (
    .in0(adder_1_out), .in1(alu_32_1_r[7:0]), .out(multiplexer_1_out), .sel(PCSel));
  Clock u_CLK (.out(CLK));
  // Probe on multiplexer_1_out
  Register register_1 (.D(multiplexer_1_out), .clk(CLK), .Q(register_1_q), .clr(Reset));  // open: en
  // Probe on adder_1_out
  ROM #(.dataWidth(32)) rom_1 (.addr(register_1_q), .data(rom_1_data));
  // Probe on register_1_q
  Adder adder_1 (.a(8'h1), .b(register_1_q), .out(adder_1_out));  // open: cin, cout
  // Probe on rom_1_data
  // Probe on rom_1_data[11:7]
  // Probe on rom_1_data[19:15]
  // Probe on rom_1_data[24:20]
  // Probe on multiplexer_4_out
  regfile_32x32_reset regfile_32x32_reset_1 (
    .DataD(multiplexer_4_out), .AddrD(rom_1_data[11:7]), .AddrA(rom_1_data[19:15]),
    .AddrB(rom_1_data[24:20]), .RegWEn(RegWEn), .clk(CLK), .Reset(Reset),
    .Reg_rs1(regfile_32x32_reset_1_reg_rs1), .x0(out_11), .x1(out_12), .x2(out_13), .x3(out_14), .x4(out_15),
    .x5(out_16), .x6(out_17), .x7(out_18), .Reg_rs2(regfile_32x32_reset_1_reg_rs2), .x8(out_19), .x9(out_20),
    .x10(out_21), .x11(out_22), .x12(out_23), .x13(out_25), .x14(out_27), .x15(out_28));
  ImmGen_v3 immgen_v3_1 (.Inst(rom_1_data), .ImmSel(ImmSel), .ExtImm(immgen_v3_1_extimm));
  // Probe on regfile_32x32_reset_1_reg_rs2
  // Probe on immgen_v3_1_extimm
  Multiplexer #(.enable("false"), .width(32)) multiplexer_2 (
    .in0(regfile_32x32_reset_1_reg_rs1), .in1({{24{1'b0}}, register_1_q}), .out(multiplexer_2_out), .sel(ASel));
  Multiplexer #(.enable("false"), .width(32)) multiplexer_3 (
    .in0(regfile_32x32_reset_1_reg_rs2), .in1(immgen_v3_1_extimm), .out(multiplexer_3_out), .sel(BSel));
  // Probe on multiplexer_2_out
  // Probe on multiplexer_3_out
  BranchComp branchcomp_1 (
    .A(regfile_32x32_reset_1_reg_rs1), .B(regfile_32x32_reset_1_reg_rs2), .BrUn(BrUn), .BrEq(BrEq),
    .BrLT(BrLT));
  ALU_32 alu_32_1 (.A(multiplexer_2_out), .B(multiplexer_3_out), .S(ALUSel), .R(alu_32_1_r));
  // Probe on alu_32_1_r
  // Probe on alu_32_1_r[9:2]
  RAM #(.asyncread("true"), .dataWidth(32)) DMEM (
    .addr(alu_32_1_r[9:2]), .we(MemRW), .oe(1'b1), .clk(CLK), .din(regfile_32x32_reset_1_reg_rs2),
    .dout(DMEM_dout));
  Multiplexer #(.enable("false"), .width(32)) multiplexer_4 (
    .in0(DMEM_dout), .in1(alu_32_1_r), .out(multiplexer_4_out), .sel(WBSel));
  // Probe on DMEM_dout

  // Other names for the same wires on the sheet: x0[31:0] = out_11; x1[31:0] = out_12; x2[31:0] = out_13;
  //   x3[31:0] = out_14; x4[31:0] = out_15; x5[31:0] = out_16; x6[31:0] = out_17; x7[31:0] = out_18;
  //   x8[31:0] = out_19; x9[31:0] = out_20; x10[31:0] = out_21; x11[31:0] = out_22; x12[31:0] = out_23;
  //   x13[31:0] = out_25; x14[31:0] = out_27; x15[31:0] = out_28

  // Notes on the sheet:
  //   Control Input Signals
  //   contents of rom_1 (hex, n*v repeats v):
  //   93 8463 100133 7ff00193 c663 40300133 ff1f293 811213 13
  //   Control Signals
  //   Only lw, no lb or lh since word (not byte) address is used by RAM
endmodule

module ImmGen_v3 (
  input  [31:0] Inst,
  input  [2:0] ImmSel,
  output [31:0] ExtImm
);

  wire [11:0] multiplexer_1_out;
  wire [19:0] multiplexer_2_out;
  wire [20:0] multiplexer_3_out;

  Multiplexer #(.enable("false"), .width(12)) multiplexer_1 (
    .in0(Inst[31:20]), .in1({Inst[31:25], Inst[11:7]}), .out(multiplexer_1_out), .sel(ImmSel[0]));
  Multiplexer #(.enable("false"), .width(20)) multiplexer_2 (
    .in0({20{1'b0}}), .in1({20{1'b1}}), .out(multiplexer_2_out), .sel(multiplexer_1_out[11]));
  Multiplexer #(.enable("false"), .width(21)) multiplexer_3 (
    .in0({21{1'b0}}), .in1({21{1'b1}}), .out(multiplexer_3_out), .sel(Inst[31]));
  Multiplexer #(.enable("false"), .select(3), .width(32)) multiplexer_4 (
    .in0({multiplexer_2_out, multiplexer_1_out}), .in1({multiplexer_2_out, multiplexer_1_out}),
    .in2({multiplexer_3_out, Inst[31], Inst[7], Inst[30:25], Inst[11:9]}), .out(ExtImm), .sel(ImmSel));  // open: in3, in4, in5, in6, in7

  // Notes on the sheet:
  //   Hence, we need to divide RV32 offset by 4.
  //   When ImmSel=010, we calculate the offset to PC. For Logisim, PC is by default incremented by 1, not 4.
endmodule

module BranchComp (
  input  [31:0] A,
  input  [31:0] B,
  input  BrUn,
  output BrEq,
  output BrLT
);

  wire comparator_1_lt, comparator_2_lt;

  Comparator #(.width(32)) comparator_1 (.a(A), .b(B), .eq(BrEq), .lt(comparator_1_lt));  // open: gt
  Comparator #(.mode("unsigned"), .width(32)) comparator_2 (.a(A), .b(B), .lt(comparator_2_lt));  // open: gt, eq
  Multiplexer #(.enable("false")) multiplexer_1 (.in0(comparator_1_lt), .in1(comparator_2_lt), .out(BrLT), .sel(BrUn));

  // Notes on the sheet:
  //   unsigned
endmodule
