// Logisim project transistor_gates.circ as structural Verilog: 23 circuits, main circuit main
module main (
  input  A,
  input  B,
  input  C,
  output Y
);

  wire and_cmos_1_c, and_cmos_2_c;

  and_cmos and_cmos_1 (.A(A), .B(B), .C(and_cmos_1_c));
  and_cmos and_cmos_2 (.A(A), .B(C), .C(and_cmos_2_c));
  or_cmos or_cmos_1 (.A(and_cmos_1_c), .B(and_cmos_2_c), .C(Y));

  // Notes on the sheet:
  //   Hiearchical design
endmodule

module inverter_cmos (
  input  X,
  output Y
);

  Transistor transistor_1 (.in(1'b1), .out(Y), .gate(X));
  Transistor #(.\type ("n")) transistor_2 (.in(1'b0), .out(Y), .gate(X));

  // Notes on the sheet:
  //   Inverter
endmodule

module nand_cmos (
  input  A,
  input  B,
  output C
);

  wire transistor_4_out;

  Transistor transistor_1 (.in(1'b1), .out(C), .gate(A));
  Transistor #(.gate("br")) transistor_2 (.in(1'b1), .out(C), .gate(B));
  Transistor #(.\type ("n")) transistor_3 (.in(transistor_4_out), .out(C), .gate(A));
  Transistor #(.\type ("n")) transistor_4 (.in(1'b0), .out(transistor_4_out), .gate(B));
endmodule

module and_cmos (
  input  A,
  input  B,
  output C
);

  wire nand_cmos_1_c;

  nand_cmos nand_cmos_1 (.A(A), .B(B), .C(nand_cmos_1_c));
  LED led_1 (.in(C));
  inverter_cmos inverter_cmos_1 (.X(nand_cmos_1_c), .Y(C));
endmodule

module or_cmos (
  input  A,
  input  B,
  output C
);

  wire inverter_cmos_1_y, inverter_cmos_2_y;

  inverter_cmos inverter_cmos_1 (.X(A), .Y(inverter_cmos_1_y));
  inverter_cmos inverter_cmos_2 (.X(B), .Y(inverter_cmos_2_y));
  LED led_1 (.in(C));
  nand_cmos nand_cmos_1 (.A(inverter_cmos_1_y), .B(inverter_cmos_2_y), .C(C));
endmodule

module not_cmos (
  input  A,
  output Y
);

  nand_cmos nand_cmos_1 (.A(A), .B(1'b1), .C(Y));
endmodule

module adder_c (
  input  [3:0] A,
  input  [3:0] B,
  output [3:0] C
);

  Adder #(.width(4)) adder_1 (.a(A), .b(B), .out(C));  // open: cin, cout
endmodule

module gate_delay (
  input  A,
  output Y
);

  wire not_1_out, not_2_out, not_3_out, not_4_out;

  not not_1 (not_1_out, A);
  // Probe on not_1_out
  not not_2 (not_2_out, not_1_out);
  // Probe on not_2_out
  not not_3 (not_3_out, not_2_out);
  // Probe on not_3_out
  not not_4 (not_4_out, not_3_out);
  // Probe on not_4_out
  not not_5 (Y, not_4_out);
endmodule

module register_c (
  input  [3:0] D,
  input  Reset,
  input  We,
  output [3:0] Q,
  output [3:0] Q2
);

  wire clock_1_out;

  Clock clock_1 (.out(clock_1_out));
  D_Flip_Flop d_ff_1 (.D(D[0]), .clk(clock_1_out), .Q(Q[0]), .reset(Reset));  // open: Qn, preset
  D_Flip_Flop d_ff_2 (.D(D[1]), .clk(clock_1_out), .Q(Q[1]), .reset(Reset));  // open: Qn, preset
  D_Flip_Flop d_ff_3 (.D(D[2]), .clk(clock_1_out), .Q(Q[2]), .reset(Reset));  // open: Qn, preset
  D_Flip_Flop d_ff_4 (.D(D[3]), .clk(clock_1_out), .Q(Q[3]), .reset(Reset));  // open: Qn, preset
  Register #(.width(4)) register_1 (.D(D), .en(We), .clk(clock_1_out), .Q(Q2), .clr(Reset));

  // Notes on the sheet:
  //   4-bit Register
  //   Four 1-bit D-FFs
endmodule

module DFF_c (
  input  S_async,
  input  D,
  input  R_async,
  output out_4,
  output out_5,
  output Q,
  output Qb
);

  wire CLK_out, clock_1_out, Master_Latch_q, not_1_out;

  Clock clock_1 (.out(clock_1_out));
  not not_1 (not_1_out, clock_1_out);
  Clock CLK (.out(CLK_out));
  D_Flip_Flop d_ff_1 (.D(D), .clk(CLK_out), .Q(Q), .Qn(Qb), .preset(S_async), .reset(R_async));
  D_latch Master_Latch (.D(D), .CLK(not_1_out), .Q(Master_Latch_q));  // open: Qb
  D_latch Slave_Latch (.D(Master_Latch_q), .CLK(clock_1_out), .Q(out_4), .Qb(out_5));

  // Notes on the sheet:
  //   D-FF from our own D-Latch
  //   D-FF provided in Logisim
endmodule

module D_latch (
  input  D,
  input  CLK,
  output Q,
  output Qb
);

  wire and_1_out, and_2_out, not_1_out;

  not not_1 (not_1_out, D);
  // Probe on and_1_out
  and and_1 (and_1_out, CLK, not_1_out);
  and and_2 (and_2_out, CLK, D);
  // Probe on and_2_out
  SR_latch sr_latch_1 (.R(and_1_out), .S(and_2_out), .Q(Q), .Qb(Qb));

  // Notes on the sheet:
  //   D-Latch created from our own SR Latch
endmodule

module SR_latch (
  input  R,
  input  S,
  output Q,
  output Qb
);

  nor nor_1 (Q, R, Qb);
  nor nor_2 (Qb, Q, S);
endmodule

module SR_latch_NAND (
  input  R,
  input  S,
  output Q,
  output Qb
);

  nand nand_1 (Q, R, Qb);
  nand nand_2 (Qb, Q, S);
endmodule

module sum (
  input  [3:0] Xi,
  input  Reset,
  output [3:0] Si,
  output [3:0] Si_1
);

  wire clock_1_out;

  Adder #(.width(4)) adder_1 (.a(Xi), .b(Si_1), .out(Si));  // open: cin, cout
  Clock clock_1 (.out(clock_1_out));
  Register #(.width(4)) register_1 (.D(Si), .clk(clock_1_out), .Q(Si_1), .clr(Reset));  // open: en
endmodule

module Detect3ones_CL (
  input  S1,
  input  S0,
  input  D,
  output nS1,
  output nS0,
  output Y
);

  wire not_1_out, not_2_out;

  not not_1 (not_1_out, S1);
  not not_2 (not_2_out, S0);
  and and_1 (nS1, not_1_out, S0, D);
  and and_2 (nS0, not_1_out, not_2_out, D);
  and and_3 (Y, S1, not_2_out, D);
endmodule

module Detect3ones_FSM (
  input  D,
  input  Reset,
  output Y
);

  wire clock_1_out, d_ff_1_q, d_ff_2_q, detect3ones_cl_1_ns0, detect3ones_cl_1_ns1;

  Detect3ones_CL detect3ones_cl_1 (
    .S1(d_ff_1_q), .S0(d_ff_2_q), .D(D), .nS1(detect3ones_cl_1_ns1), .nS0(detect3ones_cl_1_ns0), .Y(Y));
  // Probe on detect3ones_cl_1_ns0
  Clock clock_1 (.out(clock_1_out));
  // Probe on detect3ones_cl_1_ns1
  D_Flip_Flop d_ff_1 (.D(detect3ones_cl_1_ns1), .clk(clock_1_out), .Q(d_ff_1_q), .reset(Reset));  // open: Qn, preset
  D_Flip_Flop d_ff_2 (.D(detect3ones_cl_1_ns0), .clk(clock_1_out), .Q(d_ff_2_q), .reset(Reset));  // open: Qn, preset
  // Probe on d_ff_1_q
  // Probe on d_ff_2_q
endmodule

module Detect3ones_FSM2 (
  input  D,
  input  Reset,
  output Y
);

  wire clock_1_out;
  wire [1:0] detect3ones_cl_1_ns0, S;

  Detect3ones_CL detect3ones_cl_1 (
    .S1(S[1]), .S0(S[0]), .D(D), .nS1(detect3ones_cl_1_ns0[1]), .nS0(detect3ones_cl_1_ns0[0]), .Y(Y));
  Clock clock_1 (.out(clock_1_out));
  // Probe on detect3ones_cl_1_ns0
  Register #(.width(2)) register_1 (.D(detect3ones_cl_1_ns0), .clk(clock_1_out), .Q(S), .clr(Reset));  // open: en
  // Probe on S
endmodule

module nor_cmos (
  input  A,
  input  B,
  output C
);

  wire transistor_1_out;

  Transistor transistor_1 (.in(1'b1), .out(transistor_1_out), .gate(A));
  Transistor transistor_2 (.in(transistor_1_out), .out(C), .gate(B));
  Transistor #(.\type ("n")) transistor_3 (.in(1'b0), .out(C), .gate(B));
  Transistor #(.\type ("n")) transistor_4 (.in(1'b0), .out(C), .gate(A));
endmodule

module and_cmos2 (
  input  A,
  input  B,
  output C
);

  wire inverter_cmos_1_y, inverter_cmos_2_y;

  inverter_cmos inverter_cmos_1 (.X(A), .Y(inverter_cmos_1_y));
  inverter_cmos inverter_cmos_2 (.X(B), .Y(inverter_cmos_2_y));
  LED led_1 (.in(C));
  nor_cmos nor_cmos_1 (.A(inverter_cmos_1_y), .B(inverter_cmos_2_y), .C(C));
endmodule

module and_or (
  input  A,
  input  B,
  input  C,
  output Y,
  output W
);

  wire and_1_out, and_2_out;

  and and_1 (and_1_out, A, B);
  and and_2 (and_2_out, A, ~B, C);  // AND_Gate
  or or_1 (Y, and_1_out, and_2_out);
  or or_2 (W, ~and_1_out, C);  // OR_Gate
endmodule

module MOSes (
  input  in_1,
  input  in_2,
  input  in_3,
  input  in_4,
  input  in_5,
  input  in_6,
  input  in_7,
  input  in_8,
  input  in_9,
  output out_10,
  output out_11,
  output out_12,
  output out_13,
  output out_14,
  output out_15
);

  Transistor transistor_1 (.in(out_12), .out(in_5), .gate(in_4));
  Transistor #(.\type ("n")) transistor_2 (.in(out_13), .out(in_6), .gate(in_4));
  Transistor transistor_3 (.in(in_2), .out(out_10), .gate(in_1));
  Transistor #(.\type ("n")) transistor_4 (.in(in_3), .out(out_11), .gate(in_1));
  Transistor transistor_5 (.in(in_8), .out(out_14), .gate(in_7));
  Pull_Resistor pull_resistor_1 (.node(out_14));
  Transistor #(.\type ("n")) transistor_6 (.in(in_9), .out(out_15), .gate(in_7));
  Pull_Resistor #(.pull(1)) pull_resistor_2 (.node(out_15));

  // Notes on the sheet:
  //   Wrong directions of the p-MOS and n-MOS. The outputs are always U.
  //   The U (undeterminisitic) values can be pulled low or high using pullup resistor
  //   Anyway, we normally use the p and n MOSs in a pair, just like in the inverter and NAND.
endmodule

module nand_cmos_wrong (
  input  A,
  input  B,
  output C
);

  wire transistor_2_out, transistor_3_out;

  Transistor transistor_1 (.in(1'b1), .out(C), .gate(A));
  Transistor #(.\type ("n")) transistor_2 (.in(C), .out(transistor_2_out), .gate(A));
  Transistor #(.\type ("n")) transistor_3 (.in(transistor_2_out), .out(transistor_3_out), .gate(B));
  Transistor #(.gate("br")) transistor_4 (.in(1'b1), .out(C), .gate(B));
  // also tied to GND on the sheet: transistor_3_out

  // Notes on the sheet:
  //   The direction of the n-MOS's are not correct.
endmodule

module majority (
  input  a,
  input  b,
  input  c,
  output y
);

  wire and_1_out, and_2_out, and_3_out;

  and and_1 (and_1_out, b, c);
  and and_2 (and_2_out, a, c);
  or or_1 (y, and_1_out, and_2_out, and_3_out);
  and and_3 (and_3_out, a, b);
endmodule
